# Fritzing sketch pizw-nrf24-1 (saved by Fritzing 0.9.4)
breadboards: 1

parts:
  MCU1 = Raspberry Pi Zero
  Part2 = NRF24L01+ Breakout Board

nets:
  N1: MCU1.pin_1, Part2.VCC
  N2: MCU1.pin_6, Part2.GND
  N3: MCU1.pin_21, Part2.MISO
  N4: MCU1.pin_22, Part2.CE
  N5: MCU1.pin_23, Part2.SCK
